# Fritzing sketch QuickyBot (saved by Fritzing 0.9.3b)

parts:
  WeMos_D1_Mini_Battery_Shield1 = WeMos D1 Mini Battery Shield
  U1 = LIPO-110mAh [package=lipo-110]
  J1 = Basic Servo
  R1_150K = Resistor [tolerance=±5% resistance=220 package="0402 [SMD]"]
  Part1 = ws2812b [package="smd 2812b"]
  J2 = Basic Servo
  WeMos_D1_Mini1 = WeMos D1 Mini
  R2_470 = Resistor [tolerance=±5% resistance=220 package="0402 [SMD]"]
  hc-sr1 = hc-sr04
  R1_5_6K = Resistor [tolerance=±5% resistance=220 package=THT]
  U2 = SWITCH_SPDT [package=kps-1290]

nets:
  VCC: WeMos_D1_Mini_Battery_Shield1.5V, J1.vcc, Part1.VDD, J2.vcc, WeMos_D1_Mini1.5V, hc-sr1.VCC
  N1: WeMos_D1_Mini_Battery_Shield1.G, J2.gnd, WeMos_D1_Mini1.G
  N2: U1.+, U2.P
  N3: J1.pulse, WeMos_D1_Mini1.D5
  N4: R1_150K.Pin_0, WeMos_D1_Mini1.A0
  N5: R1_150K.Pin_1, U2.S
  N6: J2.pulse, WeMos_D1_Mini1.D6
  N7: WeMos_D1_Mini1.D2, hc-sr1.Trig
  N8: WeMos_D1_Mini1.D3, R2_470.Pin_0
  N9: WeMos_D1_Mini1.D7, hc-sr1.Echo
  N10: WeMos_D1_Mini1.D8, R1_5_6K.Pin_1

notes:
  D8 have 10K pull-down
  resistor
